# Fritzing sketch datalogger (saved by Fritzing 0.9.3b)
circuit board: 8.58786cm x 5.6606cm
breadboards: 1

parts:
  C1 = Tantalum Capacitor [capacitance=100nF package="B 3528 [SMD, tantalum]"]
  C3 = Tantalum Capacitor [capacitance=100nF package="B 3528 [SMD, tantalum]"]
  C2 = Tantalum Capacitor [capacitance=0.1nF package="B 3528 [SMD, tantalum]"]
  Power_plug1 = Power plug
  U1 = Voltage Regulator [package=v-reg_dpack]
  RESET = Pushbutton [package="[THT]"]
  R1 = Resistor [tolerance=±5% resistance=1M package="1206 [SMD]"]
  L1 = Inductor [inductance=10nH package="1206 [SMD]"]
  C4 = Ceramic Capacitor [capacitance=100nF package="1206 [SMD, multilayer]"]
  Q1 = Basic FET P-Channel [package="DPak [SMD]"]
  FTDI_Friend = male pin header, 6 pins [form="♂ (male)"]
  C5 = Ceramic Capacitor [capacitance=100nF package="1206 [SMD, multilayer]"]
  BAT1 = Battery Holders [package=battcon_20mm]
  WAKE_UP = Pushbutton [package="[THT]"]
  R2 = Resistor [tolerance=±5% resistance=10k package="1206 [SMD]"]
  C6 = Electrolytic Capacitor [capacitance=1µF package="0405 [SMD, electrolytic]"]
  OneWire = Molex Picoblade Series Header [part_number=0532610319 package=Picoblade-53261-0319]
  R4 = Resistor [tolerance=±5% resistance=4.7k package="1206 [SMD]"]
  U2 = SD_CARD_SOCKET [package=sdcard_4uconn]
  RTC = SO16w [chip_label=DS3231SN package=SO(w)]
  CPU = ATmega328 [package=tqfp]
  R3 = Resistor [tolerance=±5% resistance=10k package="1206 [SMD]"]

nets:
  GND: C1.-, C3.-, C2.-, Power_plug1.GND, U1.ADJ, RESET.Pin_3, RESET.Pin_4, C4.0, FTDI_Friend.pin1, FTDI_Friend.pin2, BAT1.-, WAKE_UP.Pin_1, WAKE_UP.Pin_2, C6.-, OneWire.3, U2.SH, U2.VSS1, U2.VSS2, RTC.5, RTC.6, RTC.7, RTC.8, RTC.9, RTC.10, RTC.11, RTC.12, RTC.13, CPU.GND
  6V: C1.+, Power_plug1.VCC, U1.IN, FTDI_Friend.pin3
  3.3V: C3.+, C2.+, U1.OUT, R1.Pin_0, L1.pin_0, Q1.source, R2.Pin_0, U2.VDD, RTC.2, CPU.VCC, CPU.AREF, R3.Pin_0
  RESET: RESET.Pin_1, RESET.Pin_2, R1.Pin_1, C5.1, CPU.PC6(_RESET)
  AVCC: L1.pin_1, C4.1, CPU.AVCC
  N1: Q1.Gate, CPU.PD5(T1)
  VSS Switched: Q1.drain, OneWire.1, R4.Pin_0
  N2: FTDI_Friend.pin4, CPU.PD0(RXD)
  N3: FTDI_Friend.pin5, CPU.PD1(TXD)
  N4: FTDI_Friend.pin6, C5.0
  N5: BAT1.+, C6.+, RTC.14
  INT/SQW: WAKE_UP.Pin_3, WAKE_UP.Pin_4, RTC.3, CPU.PC2(ADC2)
  SCL: R2.Pin_1, RTC.16, CPU.PC5(ADC5_SCL)
  DATA: OneWire.2, R4.Pin_1, CPU.PB0(ICP)
  CS: U2.CD_DAT3, CPU.PB2(SS_OC1B)
  MOSI: U2.CMD, CPU.PB3(MOSI_OC2)
  SCK: U2.CLK, CPU.PB5(SCK)
  MISO: U2.DAT0, CPU.PB4(MISO)
  32kHz: RTC.1
  SDA: RTC.15, CPU.PC4(ADC4_SDA), R3.Pin_1

notes:
  UW Datalogger, A datalogger for long term deployment. , 2
